# Fritzing sketch eastButtons (saved by Fritzing 0.9.3b)
breadboards: 1

parts:
  Part1 = Arduino Uno (Rev3)
  NEOPIXEL2 = Neopixel Strip -- Black (30/m)
  NEOPIXEL3 = Neopixel Strip -- Black (30/m)
  NEOPIXEL4 = Neopixel Strip -- Black (30/m)
  R1 = Resistor [tolerance=±5% resistance=10k package=THT]
  R2 = Resistor [tolerance=±5% resistance=10k package=THT]
  R3 = Resistor [tolerance=±5% resistance=10k package=THT]

nets:
  N1: Part1.D9_PWM, NEOPIXEL2.DI
  N2: Part1.D10_PWM/SS, NEOPIXEL3.DI
  N3: Part1.D11_PWM/MOSI, NEOPIXEL4.DI
  N4: Part1.D3_PWM, R3.Pin_0
  N5: Part1.D4, R2.Pin_0
  N6: Part1.D6_PWM, R1.Pin_0
  +5V: Part1.5V, NEOPIXEL2.+5V, NEOPIXEL3.+5V, NEOPIXEL4.+5V
  GND: Part1.GND, NEOPIXEL2.GND, NEOPIXEL3.GND, NEOPIXEL4.GND, R1.Pin_1, R2.Pin_1, R3.Pin_1

notes:
  Switches Common
  Switch 1
  Switch 2
  Switch 3
  +5V
  GND

custom parts:
  Neopixel Strip -- Black (30/m): Neopixel Strip, Black, 30 pixels per meter.
